// Logisim project 03.circ as structural Verilog: 1 circuit, main circuit main
module main (
  output Q0,
  output Q1,
  output Q2,
  output Q3
);

  wire clock_1_out, PRESET_out;

  Clock clock_1 (.out(clock_1_out));
  Button PRESET (.out(PRESET_out));
  D_Flip_Flop d_ff_1 (.clk(clock_1_out), .D(Q3), .Q(Q0), .en(PRESET_out));  // open: Qn, preset, reset
  D_Flip_Flop d_ff_2 (.clk(clock_1_out), .D(Q0), .Q(Q1), .reset(PRESET_out));  // open: Qn, preset, en
  D_Flip_Flop d_ff_3 (.clk(clock_1_out), .D(Q1), .Q(Q2), .reset(PRESET_out));  // open: Qn, preset, en
  D_Flip_Flop d_ff_4 (.clk(clock_1_out), .D(Q2), .Q(Q3), .reset(PRESET_out));  // open: Qn, preset, en
endmodule
