// Logisim project 02assincrono.circ as structural Verilog: 2 circuits, main circuit main
module main (
);

  J_K_Flip_Flop j_k_ff_1 ();  // open: J, clk, K, Q, Qn, preset, en, reset
endmodule

module JK_FF_meu (
  input  CLK_EN,
  input  EO,
  output out_3,
  output out_4,
  output out_5,
  output out_6
);

  wire and_1_out, and_2_out, CLK_out, CLR_out, controlled_buffer_1_out, j_k_ff_1_q, j_k_ff_2_q, j_k_ff_3_q,
       j_k_ff_4_q;

  Clock CLK (.out(CLK_out));
  assign controlled_buffer_1_out = CLK_EN ? CLK_out : 1'bz;  // Controlled_Buffer controlled_buffer_1
  assign out_3 = EO ? j_k_ff_1_q : 1'bz;  // Controlled_Buffer controlled_buffer_2
  J_K_Flip_Flop j_k_ff_1 (
    .J(1'b1), .clk(controlled_buffer_1_out), .K(1'b1), .Q(j_k_ff_1_q), .reset(CLR_out));  // open: Qn, preset, en
  Button CLR (.out(CLR_out));
  assign out_4 = EO ? j_k_ff_2_q : 1'bz;  // Controlled_Buffer controlled_buffer_3
  J_K_Flip_Flop j_k_ff_2 (
    .J(j_k_ff_1_q), .clk(controlled_buffer_1_out), .K(j_k_ff_1_q), .Q(j_k_ff_2_q), .reset(CLR_out));  // open: Qn, preset, en
  and and_1 (and_1_out, j_k_ff_1_q, j_k_ff_2_q);
  assign out_5 = EO ? j_k_ff_3_q : 1'bz;  // Controlled_Buffer controlled_buffer_4
  and and_2 (and_2_out, and_1_out, j_k_ff_3_q);
  J_K_Flip_Flop j_k_ff_3 (
    .J(and_1_out), .clk(controlled_buffer_1_out), .K(and_1_out), .Q(j_k_ff_3_q), .reset(CLR_out));  // open: Qn, preset, en
  assign out_6 = EO ? j_k_ff_4_q : 1'bz;  // Controlled_Buffer controlled_buffer_5
  J_K_Flip_Flop j_k_ff_4 (
    .J(and_2_out), .clk(controlled_buffer_1_out), .K(and_2_out), .Q(j_k_ff_4_q), .reset(CLR_out));  // open: Qn, preset, en
endmodule
