// Logisim project 05.circ as structural Verilog: 1 circuit, main circuit main
module main (
  input  in_1,
  output out_2
);

  wire clock_1_out, xor_1_out;

  Clock clock_1 (.out(clock_1_out));
  xor xor_1 (xor_1_out, in_1, out_2);
  T_Flip_Flop t_ff_1 (.clk(clock_1_out), .T(xor_1_out), .Q(out_2));  // open: Qn, preset, reset, en
endmodule
