// Logisim project 07.circ as structural Verilog: 1 circuit, main circuit main
module main (
  output Q0,
  output Q1,
  output Q2,
  output Q3
);

  wire and_1_out, and_2_out, clock_1_out, DOWN_out, j_k_ff_1_q, j_k_ff_1_qn, j_k_ff_2_q, j_k_ff_2_qn,
       j_k_ff_3_q, j_k_ff_3_qn, j_k_ff_4_q, j_k_ff_4_qn, not_1_out, or_1_out, s_r_ff_1_q, UP_out;

  Button UP (.out(UP_out));
  Button DOWN (.out(DOWN_out));
  Clock clock_1 (.out(clock_1_out));
  S_R_Flip_Flop s_r_ff_1 (.S(UP_out), .clk(or_1_out), .R(DOWN_out), .Q(s_r_ff_1_q));  // open: Qn, preset, reset, en
  or or_1 (or_1_out, UP_out, DOWN_out);
  not not_1 (not_1_out, s_r_ff_1_q);
  assign Q0 = s_r_ff_1_q ? j_k_ff_1_q : 1'bz;  // Controlled_Buffer controlled_buffer_1
  J_K_Flip_Flop j_k_ff_1 (
    .J(1'b1), .clk(clock_1_out), .K(1'b1), .Q(j_k_ff_1_q), .Qn(j_k_ff_1_qn), .reset(or_1_out));  // open: preset, en
  assign Q0 = not_1_out ? j_k_ff_1_qn : 1'bz;  // Controlled_Buffer controlled_buffer_2
  assign Q1 = not_1_out ? j_k_ff_2_qn : 1'bz;  // Controlled_Buffer controlled_buffer_3
  assign Q1 = s_r_ff_1_q ? j_k_ff_2_q : 1'bz;  // Controlled_Buffer controlled_buffer_4
  and and_1 (and_1_out, j_k_ff_1_q, j_k_ff_2_q);
  J_K_Flip_Flop j_k_ff_2 (
    .J(j_k_ff_1_q), .clk(clock_1_out), .K(j_k_ff_1_q), .Q(j_k_ff_2_q), .Qn(j_k_ff_2_qn), .reset(or_1_out));  // open: preset, en
  J_K_Flip_Flop j_k_ff_3 (
    .J(and_1_out), .clk(clock_1_out), .K(and_1_out), .Q(j_k_ff_3_q), .Qn(j_k_ff_3_qn), .reset(or_1_out));  // open: preset, en
  assign Q2 = not_1_out ? j_k_ff_3_qn : 1'bz;  // Controlled_Buffer controlled_buffer_5
  assign Q2 = s_r_ff_1_q ? j_k_ff_3_q : 1'bz;  // Controlled_Buffer controlled_buffer_6
  and and_2 (and_2_out, and_1_out, j_k_ff_3_q);
  assign Q3 = s_r_ff_1_q ? j_k_ff_4_q : 1'bz;  // Controlled_Buffer controlled_buffer_7
  J_K_Flip_Flop j_k_ff_4 (
    .J(and_2_out), .clk(clock_1_out), .K(and_2_out), .Q(j_k_ff_4_q), .Qn(j_k_ff_4_qn), .reset(or_1_out));  // open: preset, en
  assign Q3 = not_1_out ? j_k_ff_4_qn : 1'bz;  // Controlled_Buffer controlled_buffer_8
endmodule
