// Logisim project 01.circ as structural Verilog: 1 circuit, main circuit main
module main (
  input  EO,
  input  LOAD,
  input  D0,
  input  D1,
  input  D2,
  input  D3,
  output Q0,
  output Q1,
  output Q2,
  output Q3
);

  wire clock_1_out, CLR_out, d_ff_1_q, d_ff_2_q, d_ff_3_q, d_ff_4_q;

  Clock clock_1 (.out(clock_1_out));
  assign Q1 = EO ? d_ff_2_q : 1'bz;  // Controlled_Buffer controlled_buffer_1
  assign Q0 = EO ? d_ff_1_q : 1'bz;  // Controlled_Buffer controlled_buffer_2
  D_Flip_Flop d_ff_1 (.clk(clock_1_out), .D(D0), .Q(d_ff_1_q), .en(LOAD), .reset(CLR_out));  // open: Qn, preset
  D_Flip_Flop d_ff_2 (.clk(clock_1_out), .D(D1), .Q(d_ff_2_q), .en(LOAD), .reset(CLR_out));  // open: Qn, preset
  assign Q2 = EO ? d_ff_3_q : 1'bz;  // Controlled_Buffer controlled_buffer_3
  D_Flip_Flop d_ff_3 (.clk(clock_1_out), .D(D2), .Q(d_ff_3_q), .en(LOAD), .reset(CLR_out));  // open: Qn, preset
  assign Q3 = EO ? d_ff_4_q : 1'bz;  // Controlled_Buffer controlled_buffer_4
  D_Flip_Flop d_ff_4 (.clk(clock_1_out), .D(D3), .Q(d_ff_4_q), .en(LOAD), .reset(CLR_out));  // open: Qn, preset
  Button CLR (.out(CLR_out));
endmodule
