// Logisim project 06.circ as structural Verilog: 1 circuit, main circuit main
module main (
  input  in_1,
  output out_2
);

  wire clock_1_out, controlled_buffer_1_out, nand_1_out;

  Clock clock_1 (.out(clock_1_out));
  nand nand_1 (nand_1_out, in_1, out_2);
  assign controlled_buffer_1_out = in_1 ? nand_1_out : 1'bz;  // Controlled_Buffer controlled_buffer_1
  D_Flip_Flop d_ff_1 (.clk(clock_1_out), .D(controlled_buffer_1_out), .Q(out_2));  // open: Qn, preset, en, reset
endmodule
