// Logisim project 08.circ as structural Verilog: 1 circuit, main circuit main
module main (
  output Q3,
  output Q2,
  output Q1,
  output Q0
);

  wire clock_1_out, or_1_out, or_2_out, PRESET_out, xor_1_out;

  Clock clock_1 (.out(clock_1_out));
  Button PRESET (.out(PRESET_out));
  xor xor_1 (xor_1_out, clock_1_out, PRESET_out);
  D_Flip_Flop d_ff_1 (.clk(xor_1_out), .D(Q0), .Q(Q3), .reset(PRESET_out));  // open: Qn, preset, en
  D_Flip_Flop d_ff_2 (.clk(xor_1_out), .D(Q3), .Q(Q2), .reset(PRESET_out));  // open: Qn, preset, en
  or or_1 (or_1_out, Q2, PRESET_out);
  D_Flip_Flop d_ff_3 (.clk(xor_1_out), .D(or_1_out), .Q(Q1));  // open: Qn, preset, en, reset
  D_Flip_Flop d_ff_4 (.clk(xor_1_out), .D(or_2_out), .Q(Q0));  // open: Qn, preset, en, reset
  or or_2 (or_2_out, Q1, PRESET_out);
endmodule
